# Fritzing sketch Final_Board (saved by Fritzing 0.9.3b)
breadboards: 1

parts:
  R1 = Resistor [tolerance=±5% resistance=10k package=THT]  # not connected
  R2 = Resistor [tolerance=±5% resistance=3.3k package=THT]
  R3 = Resistor [tolerance=±5% resistance=100 package=THT]  # not connected
  R4 = Resistor [tolerance=±5% resistance=20k package=THT]  # not connected

nets:
  GND: R2.Pin_1

notes:
  Dout 0
  Dout 1
  Ain 0
  Vcc
  Ain 1
  TDS probe (+)
  TDS probe (-)
  Turbidity LED (+)
  Turbidity LED (-)
  Turbidity LDR (-)
  Turbidity LDR (+)
