# Fritzing sketch Final_Complete_schem (saved by Fritzing 0.9.3b)
breadboards: 1

parts:
  R1 = Resistor [tolerance=±5% resistance=10k package=THT]
  R2 = Resistor [tolerance=±5% resistance=3.3k package=THT]
  R3 = Resistor [tolerance=±5% resistance=100 package=THT]
  R4 = Resistor [tolerance=±5% resistance=20k package=THT]
  LED1 = LED - 5mm [color="Red (633nm)" package="5 mm [THT]"]
  R5 = Photocell (LDR) [package=THT]
  Arduino = Arduino Uno (Rev3)

nets:
  N1: R1.Pin_0, Arduino.D2
  N2: R1.Pin_1, Arduino.A3
  N3: R2.Pin_1, LED1.cathode, R5.pin_0, Arduino.GND
  N4: R3.Pin_0, Arduino.D4
  N5: R3.Pin_1, LED1.anode
  N6: R4.Pin_0, Arduino.5V
  N7: R4.Pin_1, R5.pin_1, Arduino.A1

notes:
  Dout 0
  Dout 1
  Ain 0
  Vcc
  Ain 1
  Turbidity
  TDS
